# Fritzing sketch Bathroom (saved by Fritzing 0.9.5d)

parts:
  A3 = ESP32 DevKitc V4
  S1 = Reed switch [package=THT]
  IR1 = TSOP312.., 314.. [package=THT]
  Mod1 = KY-019 5V Relay Module [package="Breakout board"]
  Mod2 = KY-019 5V Relay Module [package="Breakout board"]
  SPKR1 = Loudspeaker
  J1 = Piezo Speaker

nets:
  N1: A3.Pin_1, IR1.Vs
  N2: A3.Pin_10, SPKR1.pin2
  N3: A3.Pin_11, J1.pin2
  N4: A3.Pin_14, A3.Pin_32, A3.Pin_38, S1.pin_2, IR1.GND, Mod1.-, Mod2.-, SPKR1.pin1, J1.pin1
  N5: A3.Pin_19, Mod1.+, Mod2.+
  N6: A3.Pin_23, S1.pin_1
  N7: A3.Pin_26, IR1.Data
  N8: A3.Pin_30, Mod1.S
  N9: A3.Pin_31, Mod2.S

custom parts:
  ESP32 DevKitc V4: ESP32-DevKitC board with ESP32-WROOM-32 module. ESP32-DevKitC V4 is a small-sized ESP32-based development board produced by Espressif. Most of the pins on the ESP module are broken out to the pin headers on the board. The pins D0, D1, D2, D3, CMD and CLK are used internally for communication between ESP32 and SPI flash memory. They are grouped on both sides near the USB connector. Avoid using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
  KY-019 5V Relay Module: KY-019 5V Relay module, used to control AC circuits. (Special thanks to vanepp for fixing the PCB holes and other errors)
